// Logisim project CMFB-16.circ as structural Verilog: 5 circuits, main circuit CPU
module CPU (
  input  in_1,
  input  in_2,
  input  in_3,
  input  in_4,
  input  in_5,
  input  in_6,
  input  in_7,
  input  in_8,
  input  in_9,
  input  in_10,
  input  in_11,
  input  in_12,
  input  in_13,
  input  in_14,
  input  in_15,
  input  in_16,
  input  in_17,
  input  in_18,
  input  in_19,
  input  in_20
);

  wire ALUSrc;
  wire [3:0] AluOp;
  wire [15:0] alu_1_lowoutput, InmediateData, multiplexer_1_out, programcounter_1_counter,
       registers_1_aoutput, registers_1_boutput, reverse_1_dataoutput, reverse_2_dataoutput,
       reverse_3_dataoutput, reverse_4_dataoutput, WData;
  wire [63:16] Order;

  programCounter programcounter_1 (
    .NumberInput({in_16, in_15, in_14, in_13, in_12, in_11, in_10, in_9, in_8, in_7, in_6, in_5, in_4, in_3, in_2, in_1}),
    .DirectNumber(in_17), .RunCycle(in_18), .Clear(in_19), .Counter(programcounter_1_counter));
  LED led_1 (.in(programcounter_1_counter[0]));
  LED led_2 (.in(programcounter_1_counter[1]));
  LED led_3 (.in(programcounter_1_counter[2]));
  LED led_4 (.in(programcounter_1_counter[3]));
  LED led_5 (.in(programcounter_1_counter[4]));
  LED led_6 (.in(programcounter_1_counter[5]));
  LED led_7 (.in(programcounter_1_counter[6]));
  LED led_8 (.in(programcounter_1_counter[7]));
  LED led_9 (.in(programcounter_1_counter[8]));
  LED led_10 (.in(programcounter_1_counter[9]));
  LED led_11 (.in(programcounter_1_counter[10]));
  LED led_12 (.in(programcounter_1_counter[11]));
  LED led_13 (.in(programcounter_1_counter[12]));
  LED led_14 (.in(programcounter_1_counter[13]));
  LED led_15 (.in(programcounter_1_counter[14]));
  LED led_16 (.in(programcounter_1_counter[15]));
  LED led_17 (.in(Order[20]));
  LED led_18 (.in(Order[24]));
  LED led_19 (.in(Order[21]));
  LED led_20 (.in(Order[25]));
  LED led_21 (.in(Order[22]));
  LED led_22 (.in(Order[26]));
  LED led_23 (.in(Order[23]));
  LED led_24 (.in(Order[27]));
  ROM #(.addrWidth(16), .dataWidth(64)) rom_1 (
    .addr(reverse_1_dataoutput), .data({Order[63:43], ALUSrc, Order[41], AluOp, Order[36:16], InmediateData}));
  reverse reverse_1 (.DataInput(programcounter_1_counter), .DataOutput(reverse_1_dataoutput));
  LED led_25 (.in(Order[16]));
  LED led_26 (.in(Order[17]));
  LED led_27 (.in(Order[18]));
  LED led_28 (.in(Order[19]));
  LED led_29 (.in(InmediateData[0]));
  LED led_30 (.in(InmediateData[1]));
  LED led_31 (.in(InmediateData[2]));
  LED led_32 (.in(InmediateData[3]));
  LED led_33 (.in(InmediateData[4]));
  LED led_34 (.in(InmediateData[5]));
  LED led_35 (.in(InmediateData[6]));
  LED led_36 (.in(InmediateData[7]));
  LED led_37 (.in(InmediateData[8]));
  LED led_38 (.in(InmediateData[9]));
  LED led_39 (.in(InmediateData[10]));
  LED led_40 (.in(InmediateData[11]));
  LED led_41 (.in(InmediateData[12]));
  LED led_42 (.in(InmediateData[13]));
  LED led_43 (.in(InmediateData[14]));
  LED led_44 (.in(InmediateData[15]));
  registers registers_1 (
    .Clock(in_18), .WData(WData), .Reset(in_20), .WE(Order[41]), .WAddr(Order[19:16]), .RAddrA(Order[23:20]),
    .RAddrB(Order[27:24]), .AOutput(registers_1_aoutput), .BOutput(registers_1_boutput));
  Multiplexer #(.width(16)) multiplexer_1 (
    .in0(registers_1_boutput), .in1(InmediateData), .out(multiplexer_1_out), .sel(ALUSrc));
  reverse reverse_2 (.DataInput(registers_1_aoutput), .DataOutput(reverse_2_dataoutput));
  reverse reverse_3 (.DataInput(multiplexer_1_out), .DataOutput(reverse_3_dataoutput));
  LED led_45 (.in(AluOp[0]));
  LED led_46 (.in(AluOp[1]));
  LED led_47 (.in(AluOp[2]));
  LED led_48 (.in(AluOp[3]));
  ALU alu_1 (
    .AInput(reverse_2_dataoutput), .BInput(reverse_3_dataoutput), .Cin(1'b0), .ControlInput(AluOp),
    .LowOutput(alu_1_lowoutput));  // open: HighOutput, FlagsBus
  reverse reverse_4 (.DataInput(alu_1_lowoutput), .DataOutput(reverse_4_dataoutput));
  LED led_49 (.in(WData[0]));
  LED led_50 (.in(WData[1]));
  LED led_51 (.in(WData[2]));
  LED led_52 (.in(WData[3]));
  LED led_53 (.in(WData[4]));
  LED led_54 (.in(WData[5]));
  LED led_55 (.in(WData[6]));
  LED led_56 (.in(WData[7]));
  LED led_57 (.in(WData[8]));
  LED led_58 (.in(WData[9]));
  LED led_59 (.in(WData[10]));
  LED led_60 (.in(WData[11]));
  LED led_61 (.in(WData[12]));
  LED led_62 (.in(WData[13]));
  LED led_63 (.in(WData[14]));
  LED led_64 (.in(WData[15]));
  Multiplexer #(.width(16)) multiplexer_2 (
    .in0(reverse_4_dataoutput), .in1(InmediateData), .out(WData), .sel(Order[43]));

  // Other names for the same wires on the sheet: Order (some bits) = {ALUSrc, AluOp, InmediateData}; Clock = in_18;
  //   WAddr[3:0] = Order[19:16]; RAddrA[3:0] = Order[23:20]; RAddrB[3:0] = Order[27:24]; WE = Order[41];
  //   ResultSrc = Order[43]

  // Notes on the sheet:
  //   contents of rom_1 (hex, n*v repeats v):
  //   e000001000a e0000020005 20002130000 2a002140000 28003450000 24002160000 2c002170000 20000780000
  //   3a000890000
endmodule

module programCounter (
  input  [15:0] NumberInput,
  input  DirectNumber,
  input  RunCycle,
  input  Clear,
  output [15:0] Counter
);

  wire not_1_out;
  wire [1:0] minihalfadder_1_dataoutput, minihalfadder_2_dataoutput, minihalfadder_3_dataoutput,
       minihalfadder_4_dataoutput, minihalfadder_5_dataoutput, minihalfadder_6_dataoutput,
       minihalfadder_7_dataoutput, minihalfadder_8_dataoutput, minihalfadder_9_dataoutput,
       minihalfadder_10_dataoutput, minihalfadder_11_dataoutput, minihalfadder_12_dataoutput,
       minihalfadder_13_dataoutput, minihalfadder_14_dataoutput, minihalfadder_15_dataoutput,
       minihalfadder_16_dataoutput;
  wire [15:0] multiplexer_1_out;

  minihalfadder minihalfadder_1 (
    .AInput(Counter[0]), .BInput(minihalfadder_2_dataoutput[0]), .DataOutput(minihalfadder_1_dataoutput));
  minihalfadder minihalfadder_2 (
    .AInput(Counter[1]), .BInput(minihalfadder_3_dataoutput[0]), .DataOutput(minihalfadder_2_dataoutput));
  minihalfadder minihalfadder_3 (
    .AInput(Counter[2]), .BInput(minihalfadder_4_dataoutput[0]), .DataOutput(minihalfadder_3_dataoutput));
  minihalfadder minihalfadder_4 (
    .AInput(Counter[3]), .BInput(minihalfadder_5_dataoutput[0]), .DataOutput(minihalfadder_4_dataoutput));
  minihalfadder minihalfadder_5 (
    .AInput(Counter[4]), .BInput(minihalfadder_6_dataoutput[0]), .DataOutput(minihalfadder_5_dataoutput));
  minihalfadder minihalfadder_6 (
    .AInput(Counter[5]), .BInput(minihalfadder_7_dataoutput[0]), .DataOutput(minihalfadder_6_dataoutput));
  minihalfadder minihalfadder_7 (
    .AInput(Counter[6]), .BInput(minihalfadder_8_dataoutput[0]), .DataOutput(minihalfadder_7_dataoutput));
  minihalfadder minihalfadder_8 (
    .AInput(Counter[7]), .BInput(minihalfadder_9_dataoutput[0]), .DataOutput(minihalfadder_8_dataoutput));
  minihalfadder minihalfadder_9 (
    .AInput(Counter[8]), .BInput(minihalfadder_10_dataoutput[0]), .DataOutput(minihalfadder_9_dataoutput));
  minihalfadder minihalfadder_10 (
    .AInput(Counter[9]), .BInput(minihalfadder_11_dataoutput[0]), .DataOutput(minihalfadder_10_dataoutput));
  minihalfadder minihalfadder_11 (
    .AInput(Counter[10]), .BInput(minihalfadder_12_dataoutput[0]), .DataOutput(minihalfadder_11_dataoutput));
  minihalfadder minihalfadder_12 (
    .AInput(Counter[11]), .BInput(minihalfadder_13_dataoutput[0]), .DataOutput(minihalfadder_12_dataoutput));
  minihalfadder minihalfadder_13 (
    .AInput(Counter[12]), .BInput(minihalfadder_14_dataoutput[0]), .DataOutput(minihalfadder_13_dataoutput));
  minihalfadder minihalfadder_14 (
    .AInput(Counter[13]), .BInput(minihalfadder_15_dataoutput[0]), .DataOutput(minihalfadder_14_dataoutput));
  minihalfadder minihalfadder_15 (
    .AInput(Counter[14]), .BInput(minihalfadder_16_dataoutput[0]), .DataOutput(minihalfadder_15_dataoutput));
  minihalfadder minihalfadder_16 (.AInput(Counter[15]), .BInput(1'b1), .DataOutput(minihalfadder_16_dataoutput));
  not not_1 (not_1_out, DirectNumber);
  Register #(.width(16)) register_1 (.D(multiplexer_1_out), .en(1'b1), .clk(RunCycle), .Q(Counter), .clr(Clear));
  Multiplexer #(.width(16)) multiplexer_1 (
    .in0(NumberInput),
    .in1({minihalfadder_16_dataoutput[1], minihalfadder_15_dataoutput[1], minihalfadder_14_dataoutput[1], minihalfadder_13_dataoutput[1], minihalfadder_12_dataoutput[1], minihalfadder_11_dataoutput[1], minihalfadder_10_dataoutput[1], minihalfadder_9_dataoutput[1], minihalfadder_8_dataoutput[1], minihalfadder_7_dataoutput[1], minihalfadder_6_dataoutput[1], minihalfadder_5_dataoutput[1], minihalfadder_4_dataoutput[1], minihalfadder_3_dataoutput[1], minihalfadder_2_dataoutput[1], minihalfadder_1_dataoutput[1]}),
    .out(multiplexer_1_out), .sel(not_1_out));
endmodule

module registers (
  input  Clock,
  input  [15:0] WData,
  input  Reset,
  input  WE,
  input  [3:0] WAddr,
  input  [3:0] RAddrA,
  input  [3:0] RAddrB,
  output [15:0] AOutput,
  output [15:0] BOutput
);

  wire decoder_1_out0, decoder_1_out1, decoder_1_out2, decoder_1_out3, decoder_1_out4, decoder_1_out5,
       decoder_1_out6, decoder_1_out7, decoder_1_out8, decoder_1_out9, decoder_1_out10, decoder_1_out11,
       decoder_1_out12, decoder_1_out13, decoder_1_out14, decoder_1_out15;
  wire [15:0] R0, R1, R2, R3, R4, R5, R6, R7, R8, R9, R10, R11, R12, R13, R14, R15;

  Decoder #(.select(4)) decoder_1 (
    .out0(decoder_1_out0), .out1(decoder_1_out1), .out2(decoder_1_out2), .out3(decoder_1_out3),
    .out4(decoder_1_out4), .out5(decoder_1_out5), .out6(decoder_1_out6), .out7(decoder_1_out7),
    .out8(decoder_1_out8), .out9(decoder_1_out9), .out10(decoder_1_out10), .out11(decoder_1_out11),
    .out12(decoder_1_out12), .out13(decoder_1_out13), .out14(decoder_1_out14), .out15(decoder_1_out15),
    .sel(WAddr), .en(WE));
  Register #(.width(16)) register_1 (.D(WData), .en(decoder_1_out0), .clk(Clock), .Q(R0), .clr(Reset));
  Register #(.width(16)) register_2 (.D(WData), .en(decoder_1_out1), .clk(Clock), .Q(R1), .clr(Reset));
  Register #(.width(16)) register_3 (.D(WData), .en(decoder_1_out2), .clk(Clock), .Q(R2), .clr(Reset));
  Register #(.width(16)) register_4 (.D(WData), .en(decoder_1_out3), .clk(Clock), .Q(R3), .clr(Reset));
  Register #(.width(16)) register_5 (.D(WData), .en(decoder_1_out4), .clk(Clock), .Q(R4), .clr(Reset));
  Register #(.width(16)) register_6 (.D(WData), .en(decoder_1_out5), .clk(Clock), .Q(R5), .clr(Reset));
  Register #(.width(16)) register_7 (.D(WData), .en(decoder_1_out6), .clk(Clock), .Q(R6), .clr(Reset));
  Register #(.width(16)) register_8 (.D(WData), .en(decoder_1_out7), .clk(Clock), .Q(R7), .clr(Reset));
  Register #(.width(16)) register_9 (.D(WData), .en(decoder_1_out8), .clk(Clock), .Q(R8), .clr(Reset));
  Register #(.width(16)) register_10 (.D(WData), .en(decoder_1_out9), .clk(Clock), .Q(R9), .clr(Reset));
  Register #(.width(16)) register_11 (.D(WData), .en(decoder_1_out10), .clk(Clock), .Q(R10), .clr(Reset));
  Register #(.width(16)) register_12 (.D(WData), .en(decoder_1_out11), .clk(Clock), .Q(R11), .clr(Reset));
  Register #(.width(16)) register_13 (.D(WData), .en(decoder_1_out12), .clk(Clock), .Q(R12), .clr(Reset));
  Register #(.width(16)) register_14 (.D(WData), .en(decoder_1_out13), .clk(Clock), .Q(R13), .clr(Reset));
  Register #(.width(16)) register_15 (.D(WData), .en(decoder_1_out14), .clk(Clock), .Q(R14), .clr(Reset));
  Register #(.width(16)) register_16 (.D(WData), .en(decoder_1_out15), .clk(Clock), .Q(R15), .clr(Reset));
  Multiplexer #(.select(4), .width(16)) multiplexer_1 (
    .in0(R0), .in1(R1), .in2(R2), .in3(R3), .in4(R4), .in5(R5), .in6(R6), .in7(R7), .in8(R8), .in9(R9),
    .in10(R10), .in11(R11), .in12(R12), .in13(R13), .in14(R14), .in15(R15), .out(AOutput), .sel(RAddrA));
  Multiplexer #(.select(4), .width(16)) multiplexer_2 (
    .in0(R0), .in1(R1), .in2(R2), .in3(R3), .in4(R4), .in5(R5), .in6(R6), .in7(R7), .in8(R8), .in9(R9),
    .in10(R10), .in11(R11), .in12(R12), .in13(R13), .in14(R14), .in15(R15), .out(BOutput), .sel(RAddrB));
endmodule

module emptyALU (
  input  [15:0] AInput,
  input  [15:0] BInput,
  input  Cin,
  input  [3:0] ControlInput,
  output [15:0] HighOutput,
  output [15:0] LowOutput,
  output [5:0] FlagsBus
);
endmodule

module decode (
  input  [15:0] Instruction,
  output [3:0] ALUOp,
  output WE,
  output ALUSrc,
  output ResultSrc,
  output MemWrite,
  output Branch,
  output Jump
);

  ROM #(.addrWidth(16), .dataWidth(10)) rom_1 (
    .addr(Instruction), .data({Jump, Branch, MemWrite, ResultSrc, ALUSrc, WE, ALUOp}));

  // Notes on the sheet:
  //   contents of rom_1 (hex, n*v repeats v):
  //   1f 50 f
endmodule
